# Fritzing sketch Cansat fr (saved by Fritzing 0.9.3b)
breadboards: 1

parts:
  Componente1 = MPL3115A2 I2C Barometric Pressure, Altitude, Temperature Sensor
  Componente2 = u-blox NEO-6M GPS Breakout
  Componente4 = Arduino Nano 33 BLE Sense
  U1 = ESP32-38PinWide [part_number=ESP32-38PinWide]
  Componente5 = MicroSD Card Module  # not connected
  Componente6 = Adafruit RFM69HCW Transceiver Radio [part_number="Adafruit #3070 and #3071"]
  BAT1 = 6v battery [package=battery]

nets:
  GND: Componente1.GND, Componente2.GND, U1.GND, Componente6.GND, BAT1.-
  N1: Componente1.SCL, Componente4.A6, Componente4.A5
  N2: Componente1.SDA, Componente4.A4, Componente4.A3
  N3: Componente4.D3~, Componente4.D4, Componente6.SCK
  N4: Componente4.D10~, Componente4.D11/MOSI, Componente4.+5V, Componente6.MOSI
  N5: Componente4.D12~/MISO, Componente6.MISO

custom parts:
  MPL3115A2 I2C Barometric Pressure, Altitude, Temperature Sensor: This pressure sensor from Freescale is a great low-cost sensing solution for precision measurement of barometric pressure and altitude. The MPL3115A2 has a typical 1.5 Pascal resolution, which can resolve altitude at 0.3 meters (compare to the BMP180 which can do 0.17m). It has some upsides compared to the BMP180, such as interrupt outputs for ultra-low power usage, and its also a heck of a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
  Arduino Nano 33 BLE Sense: The Nano 33 BLE Sense (without headers) is Arduino’s 3.3V AI enabled board in the smallest available form factor: 45x18mm! The Arduino Nano 33 BLE Sense is a completely new board on a well-known form factor. It comes with a series of embedded sensors: 9 axis inertial sensor: what makes this board ideal for wearable devices humidity, and temperature sensor: to get highly accurate measurements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
  ESP32-38PinWide: Generic 38-Pin ESP32 with wide format (only access to one side of pins on a breadboard) based on Stephen Lilley's HiLetgo ESP-WROOM-32 ESP32 ESP-32S Development Board.
  Adafruit RFM69HCW Transceiver Radio: Sending data over long distances is like magic, and now you can be a magician with this range of powerful and easy-to-use radio modules. Sure, sometimes you want to talk to a computer (a good time to use WiFi) or perhaps communicate with a Phone (choose Bluetooth Low Energy!) but what if you want to send data very far? Most WiFi, Bluetooth, Zigbee and other wireless chipsets use 2.4GHz, which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
  6v battery: 6V lead acid battery 12ah
